// Logisim project TareaCorta-PC Control.circ as structural Verilog: 10 circuits, main circuit main
module main (
);

  wire clock_1_out, control_unit_1_alusrc, control_unit_1_memread, control_unit_1_memtoreg,
       control_unit_1_memwrite, control_unit_1_regdst, control_unit_1_regwrite, ex_mem_1_mem_memread,
       ex_mem_1_mem_memtoreg, ex_mem_1_mem_memwrite, ex_mem_1_mem_regwrite, id_ex_1_ex_alusrc,
       id_ex_1_ex_memread, id_ex_1_ex_memtoreg, id_ex_1_ex_memwrite, id_ex_1_ex_regwrite,
       mem_wb_1_mem_regwrite_2, mem_wb_1_wb_memtoreg, pc_control_1_pcsrc;
  wire [3:0] control_unit_1_aluop, id_ex_1_ex_aluop;
  wire [4:0] ex_mem_1_mem_writereg, id_ex_1_ex_writereg, mem_wb_1_wb_writereg, multiplexer_2_out;
  wire [31:0] adder_1_out, alu_1_aluresult, bit_extender_1_out, data_memory_1_read_data,
       ex_mem_1_mem_aluresult, ex_mem_1_mem_instr, ex_mem_1_mem_rsd, ex_mem_1_mem_rtd, id_ex_1_ex_imm,
       id_ex_1_ex_instr, id_ex_1_ex_pc_4, id_ex_1_ex_rsd, id_ex_1_ex_rtd, if_id_1_id_instruction,
       if_id_1_id_pc_4, Instructions_data, mem_wb_1_mem_memdata, mem_wb_1_wb_alur, multiplexer_1_out,
       multiplexer_3_out, multiplexer_4_out, pc_control_1_nextpc, PC_q, register_file_1_d1,
       register_file_1_d2;

  Multiplexer #(.width(32), .enable("false")) multiplexer_1 (
    .in0(adder_1_out), .in1(pc_control_1_nextpc), .out(multiplexer_1_out), .sel(pc_control_1_pcsrc));
  Register #(.width(32), .Select("low")) PC (.D(multiplexer_1_out), .Q(PC_q), .clk(clock_1_out));  // open: en, clr
  Clock clock_1 (.out(clock_1_out));
  Adder #(.width(32)) adder_1 (.a(32'h4), .b(PC_q), .out(adder_1_out));  // open: cin, cout
  ROM #(.addrWidth(10), .dataWidth(32), .Select("low")) Instructions (.addr(PC_q[11:2]), .data(Instructions_data));
  IF_ID if_id_1 (
    .clock(clock_1_out), .IF_PC_4(adder_1_out), .IF_Instruction(Instructions_data),
    .ID_PC_4(if_id_1_id_pc_4), .ID_Instruction(if_id_1_id_instruction));
  assign bit_extender_1_out = {{16{1'b0}}, if_id_1_id_instruction[15:0]};  // Bit_Extender bit_extender_1
  Register_File register_file_1 (
    .d1(register_file_1_d1), .rs1(if_id_1_id_instruction[25:21]), .d2(register_file_1_d2),
    .rs2(if_id_1_id_instruction[20:16]), .Write_register(mem_wb_1_wb_writereg),
    .Write_data(multiplexer_4_out), .RegWrite(mem_wb_1_mem_regwrite_2));  // open: Clock
  Control_Unit control_unit_1 (
    .Instruction(if_id_1_id_instruction), .ALUOp(control_unit_1_aluop), .ALUSrc(control_unit_1_alusrc),
    .RegDst(control_unit_1_regdst), .RegWrite(control_unit_1_regwrite), .MemRead(control_unit_1_memread),
    .MemWrite(control_unit_1_memwrite), .MemToReg(control_unit_1_memtoreg));  // open: Clock
  Multiplexer #(.width(5), .enable("false")) multiplexer_2 (
    .in0(if_id_1_id_instruction[20:16]), .in1(if_id_1_id_instruction[15:11]), .out(multiplexer_2_out),
    .sel(control_unit_1_regdst));
  ID_EX id_ex_1 (
    .clock(clock_1_out), .ID_PC_4(if_id_1_id_pc_4), .ID_rsd(register_file_1_d1), .ID_rtd(register_file_1_d2),
    .ID_imm(bit_extender_1_out), .ID_WriteReg(multiplexer_2_out), .EX_PC_4(id_ex_1_ex_pc_4),
    .EX_rsd(id_ex_1_ex_rsd), .EX_rtd(id_ex_1_ex_rtd), .EX_imm(id_ex_1_ex_imm),
    .EX_WriteReg(id_ex_1_ex_writereg), .ID_RegWrite(control_unit_1_regwrite),
    .EX_RegWrite(id_ex_1_ex_regwrite), .ID_MemToReg(control_unit_1_memtoreg),
    .EX_MemToReg(id_ex_1_ex_memtoreg), .ID_MemRead(control_unit_1_memread), .EX_MemRead(id_ex_1_ex_memread),
    .ID_MemWrite(control_unit_1_memwrite), .EX_MemWrite(id_ex_1_ex_memwrite),
    .ID_ALUSrc(control_unit_1_alusrc), .EX_ALUSrc(id_ex_1_ex_alusrc), .ID_ALUOp(control_unit_1_aluop),
    .EX_ALUOp(id_ex_1_ex_aluop), .ID_instr(if_id_1_id_instruction), .EX_instr(id_ex_1_ex_instr));
  Multiplexer #(.width(32), .enable("false")) multiplexer_3 (
    .in0(id_ex_1_ex_rtd), .in1(id_ex_1_ex_imm), .out(multiplexer_3_out), .sel(id_ex_1_ex_alusrc));
  ALU alu_1 (
    .Operand_1(id_ex_1_ex_rsd), .Operand_2(multiplexer_3_out), .ALUOp(id_ex_1_ex_aluop),
    .ALUResult(alu_1_aluresult));  // open: Clock, ShfAmt, Zero, Less_than_zero, Greater_than_zero
  EX_MEM ex_mem_1 (
    .clock(clock_1_out), .EX_PC_4(id_ex_1_ex_pc_4), .EX_ALUResult(alu_1_aluresult),
    .EX_WriteReg(id_ex_1_ex_writereg), .EX_RegWrite(id_ex_1_ex_regwrite), .EX_MemToReg(id_ex_1_ex_memtoreg),
    .EX_MemRead(id_ex_1_ex_memread), .EX_MemWrite(id_ex_1_ex_memwrite),
    .MEM_ALUResult(ex_mem_1_mem_aluresult), .MEM_WriteReg(ex_mem_1_mem_writereg),
    .MEM_RegWrite(ex_mem_1_mem_regwrite), .MEM_MemToReg(ex_mem_1_mem_memtoreg),
    .MEM_MemRead(ex_mem_1_mem_memread), .MEM_MemWrite(ex_mem_1_mem_memwrite), .EX_rtd(id_ex_1_ex_rtd),
    .MEM_rtd(ex_mem_1_mem_rtd), .EX_instr(id_ex_1_ex_instr), .MEM_instr(ex_mem_1_mem_instr),
    .EX_rsd(id_ex_1_ex_rsd), .MEM_rsd(ex_mem_1_mem_rsd));  // open: MEM_PC_4
  PC_Control pc_control_1 (
    .ALU_Result(ex_mem_1_mem_aluresult), .Instruction(ex_mem_1_mem_instr), .PCSrc(pc_control_1_pcsrc),
    .rsd(ex_mem_1_mem_rsd), .NextPC(pc_control_1_nextpc));  // open: Clock, PC
  Data_Memory data_memory_1 (
    .Clock(clock_1_out), .Address(ex_mem_1_mem_aluresult), .Write_Data(ex_mem_1_mem_rtd),
    .MemRead(ex_mem_1_mem_memread), .MemWrite(ex_mem_1_mem_memwrite), .Read_Data(data_memory_1_read_data),
    .Instruction(ex_mem_1_mem_instr));
  MEM_WB mem_wb_1 (
    .clock(clock_1_out), .EX_MemData(data_memory_1_read_data), .MEM_ALUR(ex_mem_1_mem_aluresult),
    .MEM_WriteReg(ex_mem_1_mem_writereg), .MEM_RegWrite(ex_mem_1_mem_regwrite),
    .MEM_MemToReg(ex_mem_1_mem_memtoreg), .MEM_MemData(mem_wb_1_mem_memdata), .WB_ALUR(mem_wb_1_wb_alur),
    .WB_WriteReg(mem_wb_1_wb_writereg), .MEM_RegWrite_2(mem_wb_1_mem_regwrite_2),
    .WB_MemToReg(mem_wb_1_wb_memtoreg));
  Multiplexer #(.width(32), .enable("false")) multiplexer_4 (
    .in0(mem_wb_1_wb_alur), .in1(mem_wb_1_mem_memdata), .out(multiplexer_4_out), .sel(mem_wb_1_wb_memtoreg));

  // Notes on the sheet:
  //   MIPS pipelined 2023, CI0118 grupo 3
  //   Type I
  //   Type R
  //   LW
endmodule

module ALU (
  input  Clock,
  input  [31:0] Operand_1,
  input  [31:0] Operand_2,
  input  [4:0] ShfAmt,
  input  [3:0] ALUOp,
  output [31:0] ALUResult,
  output Zero,
  output Less_than_zero,
  output Greater_than_zero
);


  // Notes on the sheet:
  //   Entradas
  //   Control
  //   Salidas
endmodule

module Control_Unit (
  input  Clock,
  input  [31:0] Instruction,
  output [3:0] ALUOp,
  output ALUSrc,
  output RegDst,
  output RegWrite,
  output MemRead,
  output MemWrite,
  output MemToReg
);


  // Other names for the same wires on the sheet: Funct[5:0] = Instruction[5:0]; OpCode[5:0] = Instruction[31:26]

  // Notes on the sheet:
  //   Entradas
  //   Salidas
endmodule

module Data_Memory (
  input  Clock,
  input  [31:0] Address,
  input  [31:0] Write_Data,
  input  [31:0] Instruction,
  input  MemRead,
  input  MemWrite,
  output [31:0] Read_Data
);

  wire [1:0] DataSize, Offset;
  wire [3:0] multiplexer_1_out, multiplexer_2_out, multiplexer_3_out;
  wire [7:0] Byte_0_data, Byte_1_data, Byte_2_data, Byte_3_data, multiplexer_4_out;
  wire [9:0] Address_10_bits;
  wire [15:0] multiplexer_5_out;

  RAM #(.dataWidth(32), .bus("separate"), .simpleMode("false"), .Select("low")) ram_1 (
    .addr(Address[7:0]), .din(Write_Data), .data(Read_Data), .str(MemWrite), .clk(Clock));  // open: sel, ld, clr
  Multiplexer #(.select(2), .width(4), .enable("false")) multiplexer_1 (
    .in0(4'b0111), .in1(4'b1011), .in2(4'b1101), .in3(4'b1110), .out(multiplexer_1_out), .sel(Offset));
  Multiplexer #(.select(2), .width(4), .enable("false")) multiplexer_2 (
    .in0(multiplexer_1_out), .in1(multiplexer_3_out), .in2(4'b0000), .in3(4'b0000),
    .out({multiplexer_2_out[3:2], multiplexer_2_out[2], multiplexer_2_out[0]}), .sel(DataSize));
  Multiplexer #(.select(2), .width(4), .enable("false")) multiplexer_3 (
    .in0(4'b1100), .in1(4'b0000), .in2(4'b0011), .in3(4'b0000), .out(multiplexer_3_out), .sel(Offset));
  RAM #(.addrWidth(10), .bus("separate"), .Select("low")) Byte_0 (
    .addr(Address_10_bits), .din(Write_Data[7:0]), .data(Byte_0_data), .sel(multiplexer_2_out[0]), .clk(Clock));  // open: str, ld, clr
  RAM #(.addrWidth(10), .bus("separate"), .Select("low")) Byte_1 (
    .addr(Address_10_bits), .din(Write_Data[15:8]), .data(Byte_1_data), .sel(multiplexer_2_out[2]),
    .clk(Clock));  // open: str, ld, clr
  RAM #(.addrWidth(10), .bus("separate"), .Select("low")) Byte_2 (
    .addr(Address_10_bits), .din(Write_Data[23:16]), .data(Byte_2_data), .sel(multiplexer_2_out[2]),
    .clk(Clock));  // open: str, ld, clr
  RAM #(.addrWidth(10), .bus("separate"), .Select("low")) Byte_3 (
    .addr(Address_10_bits), .din(Write_Data[31:24]), .data(Byte_3_data), .sel(multiplexer_2_out[3]),
    .clk(Clock));  // open: str, ld, clr
  Multiplexer #(.select(2), .width(8), .enable("false")) multiplexer_4 (
    .in0(Byte_0_data), .in1(Byte_1_data), .in2(Byte_2_data), .in3(Byte_3_data), .out(multiplexer_4_out),
    .sel(Offset));
  Multiplexer #(.select(2), .width(16), .enable("false")) multiplexer_5 (
    .in0({Byte_1_data, Byte_0_data}), .in1({16{1'b0}}), .in2({16{1'b0}}), .in3({Byte_3_data, Byte_2_data}),
    .out(multiplexer_5_out), .sel(Offset));
  Multiplexer #(.select(2), .width(32), .enable("false")) multiplexer_6 (
    .in0({{24{1'b0}}, multiplexer_4_out}), .in1({{16{1'b0}}, multiplexer_5_out}), .in2({32{1'b0}}),
    .in3({Byte_3_data, Byte_2_data, Byte_1_data, Byte_0_data}), .out(Read_Data), .sel(DataSize));

  // Other names for the same wires on the sheet: Type[1:0] = Instruction[27:26]; Extension = Instruction[28];
  //   Load_or_Store = Instruction[29]; Load_Store[1:0] = Instruction[31:30]

  // Notes on the sheet:
  //   Entradas
  //   Data Memory 2022, CI0114 grupo 3
  //   Salidas
endmodule

// PC Ctrl
module PC_Control (
  input  Clock,
  input  [31:0] ALU_Result,
  input  [31:0] rsd,
  input  [31:0] Instruction,
  input  [31:0] PC,
  output PCSrc,
  output [31:0] NextPC
);

  wire comparator_1_eq, comparator_1_gt, comparator_1_lt, multiplexer_1_out, not_1_out, or_1_out, or_2_out;
  wire [15:0] shifter_2_out;
  wire [31:0] adder_1_out, bit_extender_1_out, shifter_1_out;

  Comparator #(.width(32), .mode("unsigned")) comparator_1 (
    .a(Instruction), .b({32{1'b0}}), .gt(comparator_1_gt), .eq(comparator_1_eq), .lt(comparator_1_lt));
  Shifter #(.width(32)) shifter_1 (.in({{6{1'b0}}, Instruction[25:0]}), .\dist (5'b00010), .out(shifter_1_out));
  Shifter #(.width(16)) shifter_2 (.in(Instruction[15:0]), .\dist (4'b0010), .out(shifter_2_out));
  assign bit_extender_1_out = {{16{1'b0}}, shifter_2_out};  // Bit_Extender bit_extender_1
  or or_1 (or_1_out, comparator_1_gt, comparator_1_eq);
  not not_1 (not_1_out, comparator_1_eq);
  or or_2 (or_2_out, comparator_1_eq, comparator_1_lt);
  Adder #(.width(32)) adder_1 (.a(bit_extender_1_out), .b(PC), .out(adder_1_out));  // open: cin, cout
  Multiplexer #(.enable("false")) multiplexer_1 (
    .in0(comparator_1_lt), .in1(or_1_out), .out(multiplexer_1_out), .sel(rsd[31]));
  Multiplexer #(.width(32), .enable("false")) multiplexer_2 (
    .in0({PC[31:28], shifter_1_out[27:0]}), .in1(adder_1_out), .out(NextPC));  // open: sel
  Multiplexer #(.select(3), .enable("false")) multiplexer_3 (
    .in1(multiplexer_1_out), .in2(1'b1), .in3(comparator_1_eq), .in4(not_1_out), .in6(or_2_out),
    .in7(comparator_1_gt), .out(PCSrc));  // open: in0, in5, sel

  // Other names for the same wires on the sheet: RT[4:0] = Instruction[20:16]; RT0 = Instruction[16];
  //   BranchCode[2:0] = Instruction[28:26]; OpCode[5:0] = Instruction[31:26]

  // Notes on the sheet:
  //   Entradas
  //   Salidas
endmodule

// Reg. File
module Register_File (
  input  Clock,
  input  [4:0] rs1,
  input  [4:0] rs2,
  input  [4:0] Write_register,
  input  [31:0] Write_data,
  input  RegWrite,
  output [31:0] d1,
  output [31:0] d2
);


  // Other names for the same wires on the sheet: rs1l[2:0] = rs1[2:0]; rs1h[1:0] = rs1[4:3]; rs2l[2:0] = rs2[2:0];
  //   rs2h[1:0] = rs2[4:3]; WRL[2:0] = Write_register[2:0]; WRH[1:0] = Write_register[4:3]

  // Notes on the sheet:
  //   Entradas
  //   Control
  //   Salidas
endmodule

module IF_ID (
  input  clock,
  input  [31:0] IF_PC_4,
  input  [31:0] IF_Instruction,
  output [31:0] ID_PC_4,
  output [31:0] ID_Instruction
);

  Register #(.width(32), .Select("low")) register_1 (.D(IF_PC_4), .Q(ID_PC_4), .clk(clock));  // open: en, clr
  Register #(.width(32), .Select("low")) register_2 (
    .D(IF_Instruction), .Q(ID_Instruction), .clk(clock));  // open: en, clr
endmodule

module ID_EX (
  input  clock,
  input  [31:0] ID_PC_4,
  input  [31:0] ID_instr,
  input  [31:0] ID_rsd,
  input  [31:0] ID_rtd,
  input  [31:0] ID_imm,
  input  [4:0] ID_WriteReg,
  input  ID_RegWrite,
  input  ID_MemToReg,
  input  ID_MemRead,
  input  ID_MemWrite,
  input  ID_ALUSrc,
  input  [3:0] ID_ALUOp,
  output [31:0] EX_PC_4,
  output [31:0] EX_instr,
  output [31:0] EX_rsd,
  output [31:0] EX_rtd,
  output [31:0] EX_imm,
  output [4:0] EX_WriteReg,
  output EX_RegWrite,
  output EX_MemToReg,
  output EX_MemRead,
  output EX_MemWrite,
  output EX_ALUSrc,
  output [3:0] EX_ALUOp
);

  Register #(.width(32), .Select("low")) register_1 (.D(ID_PC_4), .Q(EX_PC_4), .clk(clock));  // open: en, clr
  Register #(.width(32), .Select("low")) register_2 (.D(ID_instr), .Q(EX_instr), .clk(clock));  // open: en, clr
  Register #(.width(32), .Select("low")) register_3 (.D(ID_rsd), .Q(EX_rsd), .clk(clock));  // open: en, clr
  Register #(.width(32), .Select("low")) register_4 (.D(ID_rtd), .Q(EX_rtd), .clk(clock));  // open: en, clr
  Register #(.width(32), .Select("low")) register_5 (.D(ID_imm), .Q(EX_imm), .clk(clock));  // open: en, clr
  Register #(.width(5), .Select("low")) register_6 (.D(ID_WriteReg), .Q(EX_WriteReg), .clk(clock));  // open: en, clr
  Register #(.width(1), .Select("low")) register_7 (.D(ID_RegWrite), .Q(EX_RegWrite), .clk(clock));  // open: en, clr
  Register #(.width(1), .Select("low")) register_8 (.D(ID_MemToReg), .Q(EX_MemToReg), .clk(clock));  // open: en, clr
  Register #(.width(1), .Select("low")) register_9 (.D(ID_MemRead), .Q(EX_MemRead), .clk(clock));  // open: en, clr
  Register #(.width(1), .Select("low")) register_10 (.D(ID_MemWrite), .Q(EX_MemWrite), .clk(clock));  // open: en, clr
  Register #(.width(1), .Select("low")) register_11 (.D(ID_ALUSrc), .Q(EX_ALUSrc), .clk(clock));  // open: en, clr
  Register #(.width(4), .Select("low")) register_12 (.D(ID_ALUOp), .Q(EX_ALUOp), .clk(clock));  // open: en, clr

  // Notes on the sheet:
  //   MEM
  //   EX
  //   WB
  //   Control
  //   Control
endmodule

module EX_MEM (
  input  clock,
  input  [31:0] EX_PC_4,
  input  [31:0] EX_instr,
  input  [31:0] EX_rsd,
  input  [31:0] EX_ALUResult,
  input  [31:0] EX_rtd,
  input  [4:0] EX_WriteReg,
  input  EX_RegWrite,
  input  EX_MemToReg,
  input  EX_MemRead,
  input  EX_MemWrite,
  output [31:0] MEM_PC_4,
  output [31:0] MEM_instr,
  output [31:0] MEM_rsd,
  output [31:0] MEM_ALUResult,
  output [31:0] MEM_rtd,
  output [4:0] MEM_WriteReg,
  output MEM_RegWrite,
  output MEM_MemToReg,
  output MEM_MemRead,
  output MEM_MemWrite
);

  Register #(.width(32), .Select("low")) register_1 (.D(EX_instr), .Q(MEM_instr), .clr(clock));  // open: en, clk
  Register #(.width(32), .Select("low")) register_2 (.D(EX_PC_4), .Q(MEM_PC_4), .clr(clock));  // open: en, clk
  Register #(.width(32), .Select("low")) register_3 (.D(EX_rsd), .Q(MEM_rsd), .clr(clock));  // open: en, clk
  Register #(.width(32), .Select("low")) register_4 (.D(EX_rtd), .Q(MEM_rtd), .clr(clock));  // open: en, clk
  Register #(.width(32), .Select("low")) register_5 (
    .D(EX_ALUResult), .Q(MEM_ALUResult), .clk(clock));  // open: en, clr
  Register #(.width(5), .Select("low")) register_6 (.D(EX_WriteReg), .Q(MEM_WriteReg), .clr(clock));  // open: en, clk
  Register #(.width(1), .Select("low")) register_7 (.D(EX_MemToReg), .Q(MEM_MemToReg), .clr(clock));  // open: en, clk
  Register #(.width(1), .Select("low")) register_8 (.D(EX_RegWrite), .Q(MEM_RegWrite), .clr(clock));  // open: en, clk
  Register #(.width(1), .Select("low")) register_9 (.D(EX_MemWrite), .Q(MEM_MemWrite), .clr(clock));  // open: en, clk
  Register #(.width(1), .Select("low")) register_10 (.D(EX_MemRead), .Q(MEM_MemRead), .clr(clock));  // open: en, clk

  // Notes on the sheet:
  //   WB
  //   MEM
  //   Control
  //   Control
endmodule

module MEM_WB (
  input  clock,
  input  [31:0] EX_MemData,
  input  [31:0] MEM_ALUR,
  input  [4:0] MEM_WriteReg,
  input  MEM_RegWrite,
  input  MEM_MemToReg,
  output [31:0] MEM_MemData,
  output [31:0] WB_ALUR,
  output [4:0] WB_WriteReg,
  output MEM_RegWrite_2,
  output WB_MemToReg
);

  Register #(.width(32), .Select("low")) register_1 (.D(MEM_ALUR), .Q(WB_ALUR), .clr(clock));  // open: en, clk
  Register #(.width(32), .Select("low")) register_2 (.D(EX_MemData), .Q(MEM_MemData), .clr(clock));  // open: en, clk
  Register #(.width(5), .Select("low")) register_3 (.D(MEM_WriteReg), .Q(WB_WriteReg), .clr(clock));  // open: en, clk
  Register #(.width(1), .Select("low")) register_4 (.D(MEM_MemToReg), .Q(WB_MemToReg), .clr(clock));  // open: en, clk
  Register #(.width(1), .Select("low")) register_5 (
    .D(MEM_RegWrite), .Q(MEM_RegWrite_2), .clr(clock));  // open: en, clk

  // Other names for the same wires on the sheet: WB_RegWrite = MEM_RegWrite_2

  // Notes on the sheet:
  //   WB
  //   Control
  //   Control
endmodule
