// Logisim project TareaCorta1.circ as structural Verilog: 1 circuit, main circuit Register File
module Register_File (
  input  Clock,
  input  [4:0] rs,
  input  [4:0] rt,
  input  [4:0] Write_register,
  input  [31:0] Write_data,
  input  RegWrite,
  output [31:0] d1,
  output [31:0] d2
);

  wire undriven_3, undriven_7;
  wire [4:0] undriven;
  wire [7:0] demultiplexer_1_out0, demultiplexer_1_out8, demultiplexer_1_out16, demultiplexer_1_out24;
  wire [31:0] R1_q, R2_q, R3_q, R4_q, R5_q, R6_q, R7_q, R8_q, R9_q, R10_q, R11_q, R12_q, R13_q, R14_q, R15_q,
       R16_q, R17_q, R18_q, R19_q, R20_q, R21_q, R22_q, R24_q, R25_q, R26_q, R27_q, R28_q, R29_q, R30_q,
       R31_q, undriven_2, undriven_4, undriven_5, undriven_6, undriven_8, undriven_9, undriven_10,
       undriven_11, undriven_12, undriven_13, undriven_14, undriven_15, undriven_16, undriven_17,
       undriven_18, undriven_19, undriven_20, undriven_21, undriven_22, undriven_23, undriven_24,
       undriven_25, undriven_26, undriven_27, undriven_28, undriven_29, undriven_30, undriven_31,
       undriven_32, undriven_33, undriven_34, undriven_35, undriven_36, undriven_37, undriven_38;

  Demultiplexer #(.select(5), .enable("false")) demultiplexer_1 (
    .out0(demultiplexer_1_out0[0]), .out1(demultiplexer_1_out0[1]), .out2(demultiplexer_1_out0[2]),
    .out3(demultiplexer_1_out0[3]), .out4(demultiplexer_1_out0[4]), .out5(demultiplexer_1_out0[5]),
    .out6(demultiplexer_1_out0[6]), .out7(demultiplexer_1_out0[7]), .out8(demultiplexer_1_out8[0]),
    .out9(demultiplexer_1_out8[1]), .out10(demultiplexer_1_out8[2]), .out11(demultiplexer_1_out8[3]),
    .out12(demultiplexer_1_out8[4]), .out13(demultiplexer_1_out8[5]), .out14(demultiplexer_1_out8[6]),
    .out15(demultiplexer_1_out8[7]), .out16(demultiplexer_1_out16[0]), .out17(demultiplexer_1_out16[1]),
    .out18(demultiplexer_1_out16[2]), .out19(demultiplexer_1_out16[3]), .out20(demultiplexer_1_out16[4]),
    .out21(demultiplexer_1_out16[5]), .out22(demultiplexer_1_out16[6]), .out23(demultiplexer_1_out16[7]),
    .out24(demultiplexer_1_out24[0]), .out25(demultiplexer_1_out24[1]), .out26(demultiplexer_1_out24[2]),
    .out27(demultiplexer_1_out24[3]), .out28(demultiplexer_1_out24[4]), .out29(demultiplexer_1_out24[5]),
    .out30(demultiplexer_1_out24[6]), .out31(demultiplexer_1_out24[7]), .sel(undriven));  // open: in
  Register #(.width(32), .Select("low")) R8 (.D(undriven_2), .en(undriven_3), .Q(R8_q), .clk(Clock));  // open: clr
  Register #(.width(32), .Select("low")) R16 (
    .D(undriven_4), .en(demultiplexer_1_out16[7]), .Q(R16_q), .clk(Clock));  // open: clr
  Register #(.width(32), .Select("low")) R24 (
    .D(undriven_5), .en(demultiplexer_1_out24[7]), .Q(R24_q), .clk(Clock));  // open: clr
  Register #(.width(32), .Select("low")) R1 (.D(undriven_6), .en(undriven_7), .Q(R1_q), .clk(Clock));  // open: clr
  Register #(.width(32), .Select("low")) R9 (
    .D(undriven_8), .en(demultiplexer_1_out8[1]), .Q(R9_q), .clk(Clock));  // open: clr
  Register #(.width(32), .Select("low")) R17 (
    .D(undriven_9), .en(demultiplexer_1_out16[6]), .Q(R17_q), .clk(Clock));  // open: clr
  Register #(.width(32), .Select("low")) R25 (
    .D(undriven_10), .en(demultiplexer_1_out24[6]), .Q(R25_q), .clk(Clock));  // open: clr
  Register #(.width(32), .Select("low")) R2 (
    .D(undriven_11), .en(demultiplexer_1_out0[6]), .Q(R2_q), .clk(Clock));  // open: clr
  Register #(.width(32), .Select("low")) R10 (
    .D(undriven_12), .en(demultiplexer_1_out8[6]), .Q(R10_q), .clk(Clock));  // open: clr
  Register #(.width(32), .Select("low")) R18 (
    .D(undriven_13), .en(demultiplexer_1_out16[5]), .Q(R18_q), .clk(Clock));  // open: clr
  Register #(.width(32), .Select("low")) R26 (
    .D(undriven_14), .en(demultiplexer_1_out24[5]), .Q(R26_q), .clk(Clock));  // open: clr
  Register #(.width(32), .Select("low")) R3 (
    .D(undriven_15), .en(demultiplexer_1_out0[5]), .Q(R3_q), .clk(Clock));  // open: clr
  Register #(.width(32), .Select("low")) R11 (
    .D(undriven_16), .en(demultiplexer_1_out8[5]), .Q(R11_q), .clk(Clock));  // open: clr
  Register #(.width(32), .Select("low")) R19 (
    .D(undriven_17), .en(demultiplexer_1_out16[4]), .Q(R19_q), .clk(Clock));  // open: clr
  Register #(.width(32), .Select("low")) R27 (
    .D(undriven_18), .en(demultiplexer_1_out24[4]), .Q(R27_q), .clk(Clock));  // open: clr
  Register #(.width(32), .Select("low")) R5 (
    .D(undriven_23), .en(demultiplexer_1_out0[2]), .Q(R5_q), .clk(Clock));  // open: clr
  Register #(.width(32), .Select("low")) R4 (
    .D(undriven_19), .en(demultiplexer_1_out0[4]), .Q(R4_q), .clk(Clock));  // open: clr
  Register #(.width(32), .Select("low")) R12 (
    .D(undriven_20), .en(demultiplexer_1_out8[4]), .Q(R12_q), .clk(Clock));  // open: clr
  Register #(.width(32), .Select("low")) R13 (
    .D(undriven_24), .en(demultiplexer_1_out8[3]), .Q(R13_q), .clk(Clock));  // open: clr
  Register #(.width(32), .Select("low")) R20 (
    .D(undriven_21), .en(demultiplexer_1_out16[3]), .Q(R20_q), .clk(Clock));  // open: clr
  Register #(.width(32), .Select("low")) R28 (
    .D(undriven_22), .en(demultiplexer_1_out24[3]), .Q(R28_q), .clk(Clock));  // open: clr
  Register #(.width(32), .Select("low")) R6 (
    .D(undriven_27), .en(demultiplexer_1_out0[3]), .Q(R6_q), .clk(Clock));  // open: clr
  Register #(.width(32), .Select("low")) R14 (
    .D(undriven_28), .en(demultiplexer_1_out8[2]), .Q(R14_q), .clk(Clock));  // open: clr
  Register #(.width(32), .Select("low")) R22 (
    .D(undriven_29), .en(demultiplexer_1_out16[1]), .Q(R22_q), .clk(Clock));  // open: clr
  Register #(.width(32), .Select("low")) R21 (
    .D(undriven_25), .en(demultiplexer_1_out16[2]), .Q(R21_q), .clk(Clock));  // open: clr
  Register #(.width(32), .Select("low")) R29 (
    .D(undriven_26), .en(demultiplexer_1_out24[2]), .Q(R29_q), .clk(Clock));  // open: clr
  Register #(.width(32), .Select("low")) R30 (
    .D(undriven_30), .en(demultiplexer_1_out24[1]), .Q(R30_q), .clk(Clock));  // open: clr
  Register #(.width(32), .Select("low")) R7 (
    .D(undriven_31), .en(demultiplexer_1_out0[7]), .Q(R7_q), .clk(Clock));  // open: clr
  Register #(.width(32), .Select("low")) R15 (
    .D(undriven_32), .en(demultiplexer_1_out8[7]), .Q(R15_q), .clk(Clock));  // open: clr
  Register #(.width(32), .Select("low")) R23 (
    .D(undriven_33), .en(demultiplexer_1_out16[0]), .Q(R24_q), .clk(Clock));  // open: clr
  Register #(.width(32), .Select("low")) R31 (
    .D(undriven_34), .en(demultiplexer_1_out24[0]), .Q(R31_q), .clk(Clock));  // open: clr
  Multiplexer #(.select(5), .width(32), .enable("false")) multiplexer_1 (
    .in0(R1_q), .in1(R2_q), .in2(R3_q), .in3(undriven_35), .in4(R4_q), .in5(R6_q), .in6(R7_q), .in7(R8_q),
    .in8(R9_q), .in9(R10_q), .in10(R11_q), .in11(R12_q), .in12(undriven_36), .in13(R13_q), .in14(R15_q),
    .in15(R16_q), .in16(R17_q), .in17(R18_q), .in18(R19_q), .in19(R20_q), .in20(R21_q), .in21(R22_q),
    .in22(R24_q), .in23(R25_q), .in24(R26_q), .in25(R27_q), .in26(R28_q), .in27(R29_q), .in28(R30_q),
    .in29(R31_q), .in30(undriven_37), .in31(undriven_38));  // open: out, sel
  Multiplexer #(.select(5), .width(32), .enable("false")) multiplexer_2 (
    .in0(R1_q), .in1(R2_q), .in2(R3_q), .in3(undriven_35), .in4(R4_q), .in5(R6_q), .in6(R7_q), .in7(R8_q),
    .in8(R9_q), .in9(R10_q), .in10(R11_q), .in11(R12_q), .in12(undriven_36), .in13(R13_q), .in14(R15_q),
    .in15(R16_q), .in16(R17_q), .in17(R18_q), .in18(R19_q), .in19(R20_q), .in20(R21_q), .in21(R22_q),
    .in22(R24_q), .in23(R25_q), .in24(R26_q), .in25(R27_q), .in26(R28_q), .in27(R29_q), .in28(R30_q),
    .in29(R31_q), .in30(undriven_37), .in31(undriven_38));  // open: out, sel

  // Other names for the same wires on the sheet: rd[4:0] = Write_register; rdl[2:0] = Write_register[2:0];
  //   rdh[1:0] = Write_register[4:3]; rsl[2:0] = rs[2:0]; rsh[1:0] = rs[4:3]; rtl[2:0] = rt[2:0]; rth[1:0] = rt[4:3]

  // Notes on the sheet:
  //   Entradas
  //   Control
  //   Salidas
endmodule
