// Logisim project TareaCorta3_ALU.circ as structural Verilog
module ALU (
  input  Clock,
  input  [31:0] Operand_1,
  input  [31:0] Operand_2,
  input  [4:0] ShfAmt,
  input  [3:0] ALUOp,
  output [31:0] ALUResult,
  output Zero,
  output Less_than_zero,
  output Greater_than_zero
);

  wire comparator_1_lt, comparator_2_lt;
  wire [31:0] adder_1_out, adder_2_out, AND_out, bit_extender_1_out, bit_extender_2_out, NOR_out, OR_out,
       shifter_1_out, shifter_2_out, shifter_3_out, subtractor_1_out, subtractor_2_out, XOR_out;

  assign AND_out = Operand_1 & Operand_2;  // AND_Gate AND, 32 bits wide
  assign OR_out = Operand_1 | Operand_2;  // OR_Gate OR, 32 bits wide
  assign XOR_out = Operand_1 ^ Operand_2;  // XOR_Gate XOR, 32 bits wide
  Adder #(.width(32)) adder_1 (.a(Operand_1), .b(Operand_2), .out(adder_1_out));  // open: cin, cout
  Adder #(.width(32)) adder_2 (.a(Operand_1), .b(Operand_2), .out(adder_2_out));  // open: cin, cout
  Subtractor #(.width(32)) subtractor_1 (.a(Operand_1), .b(Operand_2), .out(subtractor_1_out));  // open: bin, bout
  Subtractor #(.width(32)) subtractor_2 (.a(Operand_1), .b(Operand_2), .out(subtractor_2_out));  // open: bin, bout
  assign NOR_out = ~(Operand_1 | Operand_2);  // NOR_Gate NOR, 32 bits wide
  Comparator #(.width(32)) comparator_1 (.a(Operand_1), .b(Operand_2), .lt(comparator_1_lt));  // open: gt, eq
  Comparator #(.width(32), .mode("unsigned")) comparator_2 (
    .a(Operand_1), .b(Operand_2), .lt(comparator_2_lt));  // open: gt, eq
  Shifter #(.width(32)) shifter_1 (.in(Operand_1), .\dist (ShfAmt), .out(shifter_1_out));
  Shifter #(.width(32), .shift("lr")) shifter_2 (.in(Operand_1), .\dist (ShfAmt), .out(shifter_2_out));
  Shifter #(.width(32), .shift("ar")) shifter_3 (.in(Operand_1), .\dist (ShfAmt), .out(shifter_3_out));
  Comparator #(.width(32)) comparator_3 (
    .a(Operand_1), .b(Operand_2), .gt(Greater_than_zero), .eq(Zero), .lt(Less_than_zero));
  assign bit_extender_1_out = {{31{1'b0}}, comparator_1_lt};  // Bit_Extender bit_extender_1
  assign bit_extender_2_out = {{31{1'b0}}, comparator_2_lt};  // Bit_Extender bit_extender_2
  Multiplexer #(.select(4), .width(32), .enable("false")) multiplexer_1 (
    .in1(adder_1_out), .in2(adder_2_out), .in3(subtractor_1_out), .in4(subtractor_2_out), .in5(AND_out),
    .in6(OR_out), .in7(XOR_out), .in8(NOR_out), .in9(bit_extender_1_out), .in10(bit_extender_2_out),
    .in11(shifter_1_out), .in12(shifter_2_out), .in13(shifter_3_out), .out(ALUResult), .sel(ALUOp));  // open: in0, in14, in15

  // Notes on the sheet:
  //   Entradas
  //   Control
  //   Salidas
endmodule
