// Logisim project TareaCorta_E1_Circuitos.circ as structural Verilog
module AND (
  input  A,
  input  B,
  output R
);

  wire and_1_out, transistor_1_out;

  Transistor #(.\type ("n")) transistor_1 (.in(1'b1), .out(transistor_1_out), .gate(A));
  Transistor #(.\type ("n")) transistor_2 (.in(transistor_1_out), .out(R), .gate(B));
  Transistor #(.gate("br")) transistor_3 (.in(1'b0), .out(R), .gate(B));
  Transistor transistor_4 (.in(1'b0), .out(R), .gate(A));
  and and_1 (and_1_out, A, B);
  // Probe on and_1_out

  // Notes on the sheet:
  //   A: pull=down
  //   B: pull=down
  //   Pull Up Network
  //   x
  //   x
  //   R = A x B
  //   Pull Down Network
endmodule

module NAND (
  input  A,
  input  B,
  output X
);

  wire nand_1_out, transistor_1_out, transistor_4_out;

  Transistor transistor_1 (.in(1'b1), .out(transistor_1_out), .gate(A));
  Transistor transistor_2 (.in(transistor_1_out), .out(X), .gate(B));
  Transistor #(.\type ("n")) transistor_3 (.in(transistor_4_out), .out(X), .gate(A));
  Transistor #(.\type ("n")) transistor_4 (.in(1'b0), .out(transistor_4_out), .gate(B));
  // Probe on nand_1_out
  nand nand_1 (nand_1_out, A, B);

  // Notes on the sheet:
  //   A: pull=down
endmodule

module NOR (
  input  A,
  input  B,
  output X
);

  wire nor_1_out, transistor_3_out;

  Transistor #(.\type ("n")) transistor_1 (.in(1'b0), .out(X), .gate(A));
  Transistor transistor_2 (.in(transistor_3_out), .out(X), .gate(B));
  Transistor #(.gate("br")) transistor_3 (.in(1'b1), .out(transistor_3_out), .gate(A));
  Transistor #(.\type ("n"), .gate("br")) transistor_4 (.in(1'b0), .out(X), .gate(B));
  nor nor_1 (nor_1_out, A, B);
  // Probe on nor_1_out

  // Notes on the sheet:
  //   B: pull=down
  //   A: pull=down
endmodule

module NOT (
  input  A,
  output X
);

  wire not_1_out;

  Transistor transistor_1 (.in(1'b1), .out(X), .gate(A));
  Transistor #(.\type ("n")) transistor_2 (.in(1'b0), .out(X), .gate(A));
  not not_1 (not_1_out, A);
  // Probe on not_1_out

  // Notes on the sheet:
  //   A: pull=down
endmodule

module RS (
  input  R,
  input  S,
  output Qx,
  output Qx_prime
);

  wire and_1_r, and_2_r, clock_1_out;

  Clock clock_1 (.out(clock_1_out));
  AND and_1 (.A(R), .B(clock_1_out), .R(and_1_r));
  AND and_2 (.A(clock_1_out), .B(S), .R(and_2_r));
  NOR nor_1 (.A(and_1_r), .B(Qx_prime), .X(Qx));
  NOR nor_2 (.A(Qx), .B(and_2_r), .X(Qx_prime));
endmodule

module OR (
  input  A,
  input  B,
  output X
);

  wire or_1_out, transistor_4_out, undriven;

  Transistor transistor_1 (.in(transistor_4_out), .out(X), .gate(A));
  Transistor #(.\type ("n")) transistor_2 (.in(undriven), .out(X), .gate(B));
  Transistor #(.\type ("n"), .gate("br")) transistor_3 (.in(undriven), .out(X), .gate(A));
  // Probe on or_1_out
  or or_1 (or_1_out, A, B);
  Transistor #(.gate("br")) transistor_4 (.in(1'b0), .out(transistor_4_out), .gate(B));

  // Notes on the sheet:
  //   A: pull=down
  //   X = A + B
endmodule

module XOR (
  input  A,
  input  B,
  output X
);

  wire transistor_1_out, xor_1_out;

  Transistor transistor_1 (.in(1'b1), .out(transistor_1_out), .gate(A));
  Transistor #(.\type ("n")) transistor_2 (.in(1'b0), .out(transistor_1_out), .gate(A));
  xor xor_1 (xor_1_out, A, B);
  // Probe on xor_1_out
  Transistor transistor_3 (.in(X), .out(A), .gate(B));
  Transistor #(.\type ("n")) transistor_4 (.in(transistor_1_out), .out(X), .gate(B));

  // Notes on the sheet:
  //   A: pull=down
  //   X = A'B + AB'
endmodule

module XNOR (
  input  A,
  input  B,
  output X
);

  wire xnor_1_out;

  xnor xnor_1 (xnor_1_out, A, B);
  // Probe on xnor_1_out

  // Notes on the sheet:
  //   A: pull=down
  //   X = AB + A'B'
endmodule

module Full_Adder (
  input  A,
  input  B,
  input  C,
  output S,
  output Carry
);


  // Notes on the sheet:
  //   A: pull=down
  //   C: pull=down
  //   B: pull=down
endmodule
